# Fritzing sketch U-BOAT_circuit (saved by Fritzing 0.9.3b)
breadboards: 1

parts:
  부품1 = Bluetooth HC-05 Macho
  부품2 = Arduino Uno (Rev3)

nets:
  N1: 부품1.TXD, 부품2.D7
  N2: 부품1.RXD, 부품2.D8
  VCC: 부품1.VCC, 부품2.5V
  GND: 부품1.GND, 부품2.GND
